# Fritzing sketch WakeUpLight (saved by Fritzing 0.8.3b)
breadboards: 1

parts:
  R1 = Resistor [tolerance=±5% resistance=220 package=THT]
  LED1 = LED - 5mm [color="White (8000K)" package="5 mm [THT]"]
  Part1 = Arduino Uno (Rev3)
  Q1 = npn-Powertransistor [package="TO220 [THT]"]
  R2 = Resistor [tolerance=±5% resistance=220 package=THT]
  R3 = Resistor [tolerance=±5% resistance=220 package=THT]
  R4 = Resistor [tolerance=±5% resistance=220 package=THT]
  R5 = Resistor [tolerance=±5% resistance=220 package=THT]
  R6 = Resistor [tolerance=±5% resistance=220 package=THT]
  R7 = Resistor [tolerance=±5% resistance=220 package=THT]
  R8 = Resistor [tolerance=±5% resistance=220 package=THT]
  R9 = Resistor [tolerance=±5% resistance=220 package=THT]
  LED2 = LED - 5mm [color="White (8000K)" package="5 mm [THT]"]
  LED3 = LED - 5mm [color="White (8000K)" package="5 mm [THT]"]
  LED4 = LED - 5mm [color="White (8000K)" package="5 mm [THT]"]
  LED5 = LED - 5mm [color="White (8000K)" package="5 mm [THT]"]
  LED6 = LED - 5mm [color="White (8000K)" package="5 mm [THT]"]
  LED7 = LED - 5mm [color="White (8000K)" package="5 mm [THT]"]
  LED8 = LED - 5mm [color="White (8000K)" package="5 mm [THT]"]
  LED9 = LED - 5mm [color="White (8000K)" package="5 mm [THT]"]

nets:
  N1: R1.Pin_0, Part1.VIN, R2.Pin_0, R3.Pin_0, R4.Pin_0, R5.Pin_0, R6.Pin_0, R7.Pin_0, R8.Pin_0, R9.Pin_0
  N2: R1.Pin_1, LED1.anode
  N3: LED1.cathode, Q1.collector, LED2.cathode, LED3.cathode, LED4.cathode, LED5.cathode, LED6.cathode, LED7.cathode, LED8.cathode, LED9.cathode
  N4: Part1.GND, Q1.emitter
  N5: Part1.D6_PWM, Q1.base
  N6: R2.Pin_1, LED2.anode
  N7: R3.Pin_1, LED3.anode
  N8: R4.Pin_1, LED4.anode
  N9: R5.Pin_1, LED5.anode
  N10: R6.Pin_1, LED6.anode
  N11: R7.Pin_1, LED7.anode
  N12: R8.Pin_1, LED8.anode
  N13: R9.Pin_1, LED9.anode
